// Logisim project 2380343Demux.circ as structural Verilog: 1 circuit, main circuit main
module main (
  input  S1,
  input  S0,
  input  I1,
  input  I0,
  output O3,
  output O2,
  output O1,
  output O0
);

  // _4_to_1_MUX__x2___74153 #(.Facing("east")) 4_to_1_mux_x2_74153_1: pin names not known; wires that end beside it: I1, 1'b0, 1'b0, I0, 1'b0, 1'b0, O3
  // _4_to_1_MUX__x2___74153 #(.Facing("east")) 4_to_1_mux_x2_74153_2: pin names not known; wires that end beside it: 1'b0, I1, I0, 1'b0, S0, 1'b0, S1, 1'b0, O2
  // _4_to_1_MUX__x2___74153 #(.Facing("east")) 4_to_1_mux_x2_74153_3: pin names not known; wires that end beside it: 1'b0, I0, I1, 1'b0, S0, 1'b0, S1, 1'b0, O1
  // _4_to_1_MUX__x2___74153 #(.Facing("east")) 4_to_1_mux_x2_74153_4: pin names not known; wires that end beside it: I1, I0, I0, 1'b0, 1'b0, I1, S0, 1'b0, S0, S1, 1'b0, S1, S0, O0
endmodule
