// Logisim project 2380343ENCODER.circ as structural Verilog: 1 circuit, main circuit main
module main (
  input  I0,
  input  I1,
  input  I2,
  input  I3,
  input  I4,
  input  I5,
  input  I6,
  input  I7,
  output O0,
  output O1,
  output O2
);

  wire or_1_out, or_2_out, or_3_out, or_4_out, or_5_out, or_6_out, or_7_out, or_8_out, or_9_out;

  or or_1 (or_1_out, I1, I3);
  or or_2 (or_2_out, I5, I7);
  or or_3 (or_3_out, or_1_out, or_2_out);
  not not_1 (O0, or_3_out);
  or or_4 (or_4_out, I5, I2);
  or or_5 (or_5_out, or_4_out, or_6_out);
  not not_2 (O1, or_5_out);
  or or_6 (or_6_out, I6, I3);
  or or_7 (or_7_out, I5, I4);
  or or_8 (or_8_out, I7, I6);
  or or_9 (or_9_out, or_7_out, or_8_out);
  not not_3 (O2, or_9_out);
endmodule
