// Logisim project 2380343MUX.circ as structural Verilog: 1 circuit, main circuit main
module main (
  input  S3,
  input  S2,
  input  S1,
  input  S0,
  input  \ı0 ,
  input  I1,
  input  I2,
  input  I3,
  input  I4,
  input  I5,
  input  I6,
  input  I7,
  input  I8,
  input  I9,
  input  I10,
  output out_16
);

  wire and_1_out, n4_to_1_mux_x2_74153_1_p16, n4_to_1_mux_x2_74153_1_p17, n4_to_1_mux_x2_74153_2_p18,
       not_1_out, not_2_out, or_1_out;

  not not_1 (not_1_out, S3);
  not not_2 (not_2_out, S2);
  // NOT_Gate not_3 has open pins: in=S0, out=open
  // NOT_Gate not_4 has open pins: in=S1, out=open
  // _4_to_1_MUX__x2___74153 #(.Facing("east")) 4_to_1_mux_x2_74153_1: pin names not known; wires that end beside it: \ı0 , I1, I2, I3, I4, I5, \ı0 , I1, I2, I3, I4, I5, I6, S2, not_2_out, n4_to_1_mux_x2_74153_1_p16, n4_to_1_mux_x2_74153_1_p17
  // _4_to_1_MUX__x2___74153 #(.Facing("east")) 4_to_1_mux_x2_74153_2: pin names not known; wires that end beside it: I6, I7, I7, I8, I9, I10, 1'b0, 1'b0, 1'b0, 1'b0, 1'b0, S0, not_1_out, S0, S1, 1'b0, S1, n4_to_1_mux_x2_74153_2_p18
  or or_1 (or_1_out, n4_to_1_mux_x2_74153_1_p16, n4_to_1_mux_x2_74153_1_p17);
  and and_1 (and_1_out, not_1_out, or_1_out);
  or or_2 (out_16, and_1_out, n4_to_1_mux_x2_74153_2_p18);
endmodule
