// Logisim project e2380343.circ as structural Verilog: 1 circuit, main circuit main
module main (
  input  O1,
  input  O0,
  input  S,
  input  A1,
  input  A0,
  input  B1,
  input  B0,
  output L,
  output G,
  output E,
  output B,
  output out_12,
  output out_13,
  output L0,
  output out_15,
  output out_16,
  output out_17,
  output out_18,
  output out_19,
  output out_20,
  output L1,
  output out_22,
  output out_23,
  output L2,
  output out_25,
  output out_26,
  output out_27,
  output out_28,
  output out_29,
  output out_30,
  output out_31,
  output out_32,
  output L3,
  output out_34,
  output out_35,
  output out_36,
  output out_37,
  output out_38,
  output L4,
  output out_40,
  output out_41,
  output L5,
  output out_43,
  output out_44,
  output out_45,
  output out_46,
  output out_47,
  output out_48,
  output out_49,
  output out_50,
  output out_51,
  output L6,
  output out_53,
  output out_54,
  output out_55,
  output out_56,
  output L7,
  output out_58,
  output out_59,
  output N
);

  wire and_1_out, and_2_out, and_3_out, and_4_out, and_5_out, and_6_out, and_7_out, and_8_out, and_9_out,
       and_10_out, and_11_out, and_12_out, and_13_out, and_14_out, and_15_out, and_16_out, and_17_out,
       and_18_out, and_19_out, and_20_out, and_21_out, and_22_out, and_23_out, and_24_out, and_25_out,
       and_26_out, and_27_out, and_28_out, and_29_out, and_30_out, and_31_out, and_33_out, and_34_out,
       and_35_out, and_36_out, and_37_out, and_38_out, n3_to_8_decoder_74138_2_p6,
       n3_to_8_decoder_74138_4_p14, not_1_out, not_2_out, not_3_out, not_4_out, not_5_out, not_6_out,
       not_7_out, not_8_out, not_9_out, not_10_out, not_11_out, not_12_out, not_13_out, not_14_out,
       not_15_out, not_16_out, not_17_out, not_18_out, not_19_out, not_20_out, not_21_out, not_22_out,
       not_23_out, not_25_out, not_26_out, not_27_out, not_28_out, not_29_out, not_30_out, not_31_out,
       not_32_out, not_33_out, not_34_out, not_35_out, not_36_out, not_37_out, not_38_out, not_39_out,
       not_40_out, or_1_out, or_2_out, or_3_out, or_4_out, or_5_out, or_6_out, or_7_out, or_8_out, or_9_out,
       or_10_out, or_11_out, or_12_out, or_13_out, or_14_out, or_16_out, or_17_out, or_18_out, or_19_out,
       or_21_out, or_22_out, or_23_out, or_24_out, or_25_out, or_26_out, or_27_out, or_28_out, or_29_out,
       or_30_out, or_31_out, or_32_out, or_33_out, or_34_out, or_36_out, or_37_out, or_38_out, or_40_out,
       xnor_1_out, xnor_2_out;

  not not_1 (not_1_out, O1);
  not not_2 (not_2_out, O0);
  not not_3 (not_3_out, A1);
  not not_4 (not_4_out, S);
  not not_5 (not_5_out, A0);
  not not_6 (not_6_out, B0);
  not not_7 (not_7_out, B1);
  and and_1 (and_1_out, not_4_out, not_2_out);
  // _3_to_8_decoder__74138 #(.Facing("east")) 3_to_8_decoder_74138_1: pin names not known; wires that end beside it: B0, B1, A0
  // _3_to_8_decoder__74138 #(.Facing("east")) 3_to_8_decoder_74138_2: pin names not known; wires that end beside it: B0, B1, A0, not_3_out, A1, n3_to_8_decoder_74138_2_p6, n3_to_8_decoder_74138_2_p6, 1'b0, 1'b0
  and and_2 (and_2_out, O1, O0);
  // _3_to_8_decoder__74138 #(.Facing("east")) 3_to_8_decoder_74138_3: pin names not known; wires that end beside it: B0, B1, A0
  // _3_to_8_decoder__74138 #(.Facing("east")) 3_to_8_decoder_74138_4: pin names not known; wires that end beside it: A1, not_3_out, A0, not_5_out, B1, not_7_out, B0, not_6_out, B0, B1, A0, not_3_out, A1, n3_to_8_decoder_74138_4_p14, n3_to_8_decoder_74138_4_p14, 1'b0, 1'b0
  and and_3 (and_3_out, O0, S);
  and and_4 (and_4_out, not_6_out, not_7_out);
  and and_5 (and_5_out, and_4_out, A0);
  or or_1 (or_1_out, and_5_out, and_6_out);
  and and_6 (and_6_out, A1, not_7_out);
  and and_7 (and_7_out, not_6_out, and_8_out);
  and and_8 (and_8_out, A0, A1);
  and and_9 (and_9_out, A1, B0);
  and and_10 (and_10_out, O0, not_1_out);
  and and_11 (and_11_out, not_6_out, A0);
  and and_12 (and_12_out, O1, and_1_out);
  and and_13 (and_13_out, A1, A0);
  or or_2 (or_2_out, and_13_out, and_14_out);
  and and_14 (and_14_out, A1, not_5_out);
  and and_15 (and_15_out, not_3_out, A0);
  or or_3 (or_3_out, and_15_out, and_16_out);
  and and_16 (and_16_out, not_5_out, not_3_out);
  and and_17 (and_17_out, O1, not_2_out);
  and and_18 (and_18_out, not_3_out, not_5_out);
  and and_19 (and_19_out, not_3_out, A0);
  and and_20 (and_20_out, A1, not_5_out);
  and and_21 (and_21_out, A1, A0);
  // NOT_Gate not_8 has open pins: in=open, out=not_8_out
  // NOT_Gate not_9 has open pins: in=open, out=not_9_out
  // NOT_Gate not_10 has open pins: in=open, out=not_10_out
  // NOT_Gate not_11 has open pins: in=open, out=not_11_out
  // NOT_Gate not_12 has open pins: in=open, out=not_12_out
  // NOT_Gate not_13 has open pins: in=open, out=not_13_out
  // NOT_Gate not_14 has open pins: in=open, out=not_14_out
  // NOT_Gate not_15 has open pins: in=open, out=not_15_out
  // NOT_Gate not_16 has open pins: in=open, out=not_16_out
  // NOT_Gate not_17 has open pins: in=open, out=not_17_out
  // NOT_Gate not_18 has open pins: in=open, out=not_18_out
  // NOT_Gate not_19 has open pins: in=open, out=not_19_out
  // NOT_Gate not_20 has open pins: in=open, out=not_20_out
  // NOT_Gate not_21 has open pins: in=open, out=not_21_out
  // NOT_Gate not_22 has open pins: in=open, out=not_22_out
  // NOT_Gate not_23 has open pins: in=open, out=not_23_out
  and and_22 (and_22_out, and_2_out, not_4_out);
  not not_24 (n3_to_8_decoder_74138_2_p6, and_22_out);
  // NOT_Gate not_25 has open pins: in=open, out=not_25_out
  // NOT_Gate not_26 has open pins: in=open, out=not_26_out
  // NOT_Gate not_27 has open pins: in=open, out=not_27_out
  // NOT_Gate not_28 has open pins: in=open, out=not_28_out
  // NOT_Gate not_29 has open pins: in=open, out=not_29_out
  // NOT_Gate not_30 has open pins: in=open, out=not_30_out
  // NOT_Gate not_31 has open pins: in=open, out=not_31_out
  // NOT_Gate not_32 has open pins: in=open, out=not_32_out
  // NOT_Gate not_33 has open pins: in=open, out=not_33_out
  // NOT_Gate not_34 has open pins: in=open, out=not_34_out
  // NOT_Gate not_35 has open pins: in=open, out=not_35_out
  // NOT_Gate not_36 has open pins: in=open, out=not_36_out
  // NOT_Gate not_37 has open pins: in=open, out=not_37_out
  // NOT_Gate not_38 has open pins: in=open, out=not_38_out
  // NOT_Gate not_39 has open pins: in=open, out=not_39_out
  // NOT_Gate not_40 has open pins: in=open, out=not_40_out
  and and_23 (and_23_out, O1, and_3_out);
  not not_41 (n3_to_8_decoder_74138_4_p14, and_23_out);
  and and_24 (and_24_out, not_3_out, not_5_out);
  and and_25 (and_25_out, and_24_out, B0);
  and and_26 (and_26_out, not_3_out, B1);
  and and_27 (and_27_out, B1, and_28_out);
  and and_28 (and_28_out, not_5_out, B0);
  or or_4 (or_4_out, or_1_out, and_7_out);
  or or_5 (or_5_out, and_9_out, and_11_out);
  and and_29 (and_29_out, and_12_out, or_3_out);
  and and_30 (and_30_out, and_12_out, or_2_out);
  and and_31 (and_31_out, S, and_17_out);
  or or_6 (or_6_out, not_10_out, not_16_out);
  or or_7 (or_7_out, and_25_out, and_26_out);
  or or_8 (or_8_out, or_7_out, and_27_out);
  xnor xnor_1 (xnor_1_out, A1, B1);
  xnor xnor_2 (xnor_2_out, A0, B0);
  and and_32 (B, and_10_out, or_5_out);
  or or_9 (or_9_out, and_29_out, and_34_out);
  or or_10 (or_10_out, not_9_out, not_12_out);
  and and_33 (and_33_out, and_31_out, and_19_out);
  and and_34 (and_34_out, and_31_out, and_18_out);
  or or_11 (or_11_out, not_17_out, not_20_out);
  or or_12 (or_12_out, not_25_out, not_35_out);
  and and_35 (and_35_out, xnor_1_out, xnor_2_out);
  and and_36 (and_36_out, not_2_out, not_1_out);
  or or_13 (or_13_out, or_9_out, not_8_out);
  or or_14 (or_14_out, and_30_out, or_10_out);
  and and_37 (and_37_out, and_31_out, and_20_out);
  and and_38 (and_38_out, and_31_out, and_21_out);
  or or_15 (L6, and_38_out, not_23_out);
  or or_16 (or_16_out, not_18_out, not_21_out);
  or or_17 (or_17_out, or_12_out, not_40_out);
  and and_39 (L, or_8_out, and_36_out);
  and and_40 (G, or_4_out, and_36_out);
  and and_41 (E, and_35_out, and_36_out);
  or or_18 (or_18_out, or_14_out, not_31_out);
  or or_19 (or_19_out, and_37_out, or_16_out);
  or or_20 (L5, not_22_out, not_19_out);
  or or_21 (or_21_out, or_6_out, not_13_out);
  or or_22 (or_22_out, not_33_out, not_38_out);
  or or_23 (or_23_out, not_39_out, not_34_out);
  or or_24 (or_24_out, not_32_out, not_27_out);
  or or_25 (or_25_out, not_26_out, not_36_out);
  or or_26 (or_26_out, or_13_out, not_30_out);
  or or_27 (or_27_out, or_18_out, or_23_out);
  or or_28 (or_28_out, and_33_out, or_21_out);
  or or_29 (or_29_out, or_11_out, not_14_out);
  or or_30 (or_30_out, or_29_out, not_11_out);
  or or_31 (or_31_out, not_26_out, not_27_out);
  or or_32 (or_32_out, or_31_out, not_28_out);
  or or_33 (or_33_out, or_32_out, not_31_out);
  or or_34 (or_34_out, not_36_out, or_25_out);
  or or_35 (L0, or_26_out, or_17_out);
  or or_36 (or_36_out, or_27_out, not_29_out);
  or or_37 (or_37_out, or_28_out, or_22_out);
  or or_38 (or_38_out, or_30_out, not_37_out);
  or or_39 (L4, or_19_out, not_15_out);
  or or_40 (or_40_out, or_33_out, not_32_out);
  or or_41 (N, or_40_out, not_36_out);
  or or_42 (L1, or_36_out, or_34_out);
  or or_43 (L2, or_37_out, or_24_out);
  or or_44 (L3, or_38_out, not_28_out);

  assign L7 = 1'b0;
  assign out_12 = L0;
  assign out_13 = L0;
  assign out_15 = L0;
  assign out_16 = L0;
  assign out_17 = L0;
  assign out_18 = L1;
  assign out_19 = L1;
  assign out_20 = L1;
  assign out_22 = L1;
  assign out_23 = L1;
  assign out_25 = L2;
  assign out_26 = L2;
  assign out_27 = L2;
  assign out_28 = L2;
  assign out_29 = L2;
  assign out_30 = L3;
  assign out_31 = L3;
  assign out_32 = L3;
  assign out_34 = L3;
  assign out_35 = L3;
  assign out_36 = L4;
  assign out_37 = L4;
  assign out_38 = L4;
  assign out_40 = L4;
  assign out_41 = L4;
  assign out_43 = L5;
  assign out_44 = L5;
  assign out_45 = L5;
  assign out_46 = L5;
  assign out_47 = L5;
  assign out_48 = L6;
  assign out_49 = L6;
  assign out_50 = L6;
  assign out_51 = L6;
  assign out_53 = L6;
  assign out_54 = 1'b0;
  assign out_55 = 1'b0;
  assign out_56 = 1'b0;
  assign out_58 = 1'b0;
  assign out_59 = 1'b0;
endmodule
